# Fritzing sketch mqtt_oled_i2c_nodemcu (saved by Fritzing 0.9.1b)
breadboards: 1

parts:
  U1 = NodeMCU V1.0
  Squix1 = OLED 0.96" 128x64 I2C SSD1306

nets:
  N1: U1.D1, Squix1.SCL
  N2: U1.D2, Squix1.SCA
  GND: U1.GND, Squix1.GND
  VIN: U1.Vin, Squix1.VCC

custom parts:
  NodeMCU V1.0: ESP8266 based NodeMCU
